# Fritzing sketch rainSensor (saved by Fritzing 0.9.3b)
circuit board: 7.1cm x 6.1cm
breadboards: 1

parts:
  MCP3008 = MCP3008 [part_number=gjhN package="DIP (Dual Inline) [THT]"]
  Humidity_sensor = YL-83 Rain Sensor - Control Board
  Rain_sensor = YL-83 Rain Sensor - Detection Board
  Power = HLK-PM01
  Raspberry_zero = Raspberry Pi Zero
  1 = female pin header, 1 pin [form="♀ (female)"]
  2 = female pin header, 1 pin [form="♀ (female)"]

nets:
  N1: MCP3008.1G_, Humidity_sensor.AO
  N2: MCP3008.2Y3, MCP3008.2A, Humidity_sensor.GND, Power.-Vo, Raspberry_zero.pin_6, Raspberry_zero.pin_20, Raspberry_zero.pin_25, Raspberry_zero.pin_39
  N3: MCP3008.2Y2, Raspberry_zero.pin_24
  N4: MCP3008.2Y1, Raspberry_zero.pin_19
  N5: MCP3008.2Y0, Raspberry_zero.pin_21
  N6: MCP3008.2B, Raspberry_zero.pin_23
  VCC: MCP3008.2G_, MCP3008.VCC, Humidity_sensor.VCC, Raspberry_zero.pin_1, Raspberry_zero.pin_17
  N7: Humidity_sensor.POS, Rain_sensor.POS
  N8: Humidity_sensor.NEG, Rain_sensor.NEG
  N9: Power.AC#0, 2.pin1
  N10: Power.AC#1, 1.pin1
  N11: Power.+Vo, Raspberry_zero.pin_2, Raspberry_zero.pin_4

custom parts:
  MCP3008: A Dual 2 to 4 DEMX / Decoder
  YL-83 Rain Sensor - Control Board: The YL-83 is a rain sensor that has more resistance when dry and less resistance when wet. The module runs at 5V.
  YL-83 Rain Sensor - Detection Board: The YL-83 is a rain sensor that has more resistance when dry and less resistance when wet. The module runs at 5V.
